// Digital circuit AC6309_address_decoder.dig as structural Verilog
module AC6309_address_decoder (
  input  in_1
);

  // _7400 _7400_1: pin names not known; wires that end beside it: 1'b0, 1'b0, 1'b1
  // _74138 _74138_1: pin names not known; wires that end beside it: 1'b0, 1'b1
  // _74138 _74138_2: pin names not known; wires that end beside it: 1'b0, 1'b1
  // _7404 _7404_1: pin names not known; wires that end beside it: 1'b0, 1'b1
endmodule
